# Fritzing sketch led+transistor+switch (saved by Fritzing 0.9.3b)
circuit board: 8.46667cm x 5.64444cm
breadboards: 1

parts:
  R1 = Resistor [tolerance=±5% resistance=10k package=THT]
  Q1 = NPN-Transistor [package="TO92 [THT]"]
  S1 = Pushbutton [package="[SMD]"]
  LED1 = LED - 5mm [color="Orange (620nm)" package="5 mm [THT]"]
  LED2 = LED - 5mm [color="Green (570nm)" package="5 mm [THT]"]
  R2 = Resistor [tolerance=±5% resistance=1k package="2010 [SMD]"]
  R3 = Resistor [tolerance=±5% resistance=1k package="2010 [SMD]"]

nets:
  N1: R1.Pin_0, Q1.B
  N2: R1.Pin_1, S1.Pin_3, S1.Pin_4, LED1.anode
  N3: Q1.E, S1.Pin_1, S1.Pin_2, R2.Pin_1, R3.Pin_0
  N4: Q1.C, LED2.anode
  N5: LED1.cathode, R2.Pin_0
  N6: LED2.cathode, R3.Pin_1
